# Fritzing sketch Fritzing (saved by Fritzing 0.9.4)
breadboards: 2

parts:
  M1 = DOIT Esp32 DevKit v1 (30 pins long, 11 pins width) [part_number=ESP32S-PIN30]
  Parça1 = RFID-RC522-v2
  GY1 = MPU-6050 Board GY-521 [form="♀ (female)" package=THT]
  LED1 = RGB LED (com. cathode, rbg) [package="5 mm [THT]"]
  M2 = Dagu DGServo 9g (Top view) [part_number=RS001B]
  Parça2 = Arduino Uno (Rev3)

nets:
  3V3: M1.3V3, Parça1.3.3V, GY1.pin1
  GND: M1.GND, Parça1.GND, GY1.pin2, LED1.common_cathode
  N1: M1.D18, Parça1.SCK
  N2: M1.D19, Parça1.MISO
  N3: M1.D21, Parça1.SDA, GY1.pin4
  N4: M1.D22, GY1.pin3
  N5: M1.D23, Parça1.MOSI
  N6: M1.D32, Parça1.RST
  N7: M1.D25, LED1.red_anode
  N8: M1.D26, LED1.blue_anode
  N9: M1.D27, LED1.green_anode
  N10: M1.D13, M2.pulse
  GND_2: M2.gnd, Parça2.GND
  VCC: M2.vcc, Parça2.5V

custom parts:
  DOIT Esp32 DevKit v1 (30 pins long, 11 pins width): The DOIT Esp32 DevKit v1 is one of the development board created by DOIT to evaluate the ESP-WROOM-32 module. It is based on the ESP32 microcontroller that boasts Wifi, Bluetooth, Ethernet and Low Power support all in a single chip. (vanepp) made breadboard work, adjusted pin numbering and labels and reduced size of schematic and cleaned up pcb. This chip is 30pins long (2 x15) and 11 pins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
  RFID-RC522-v2: A simple China made RFID-RC522 Reader; do check the pin labels, as this is a MFRC522 based clone.
  MPU-6050 Board GY-521: Acelerometro y Giroscopio MPU-6050 Board GY-521
